// Logisim project 2107118 ALU 22 BIT.circ as structural Verilog: 10 circuits, main circuit main
module main (
  input  [21:0] A,
  input  NAND,
  input  NOR,
  input  [21:0] B,
  input  CONTROL_0,
  input  CONTROL_1,
  output [21:0] RESULT,
  output ZERO,
  output NEGATIVE,
  output CARRY,
  output OVERFLOW
);

  wire [21:0] multiplexer_1_out, multiplexer_2_out, multiplexer_3_out, n22_bit_adder_subtractor_1_result,
       n22_bit_and_1_result, n22_bit_or_1_result, nor_1_res, xnor_1_resul;

  \xnor  xnor_1 (.A(A), .B(B), .RESUL(xnor_1_resul));
  NOR nor_1 (.A(A), .B(B), .RES(nor_1_res));
  _22_BIT_AND u_22_bit_and_1 (.A(A), .B(B), .RESULT(n22_bit_and_1_result));
  _22_BIT_OR u_22_bit_or_1 (.A(A), .B(B), .RESULT(n22_bit_or_1_result));
  _22_BIT_ADDER_SUBTRACTOR u_22_bit_adder_subtractor_1 (
    .A(A), .B(B), .C_IN(CONTROL_0), .RESULT(n22_bit_adder_subtractor_1_result), .CARRY_OUT(CARRY),
    .OVERFLOW(OVERFLOW));
  Multiplexer #(.width(22)) multiplexer_1 (
    .in0(n22_bit_and_1_result), .in1(n22_bit_or_1_result), .out(multiplexer_1_out), .sel(CONTROL_0));  // open: en
  Multiplexer #(.width(22)) multiplexer_2 (
    .in0(multiplexer_1_out), .in1(n22_bit_adder_subtractor_1_result), .out(multiplexer_2_out), .sel(CONTROL_1));  // open: en
  Multiplexer #(.width(22), .enable("false")) multiplexer_3 (
    .in0(multiplexer_2_out), .in1(xnor_1_resul), .out(multiplexer_3_out), .sel(NAND));
  Multiplexer #(.width(22), .enable("false")) multiplexer_4 (
    .in0(multiplexer_3_out), .in1(nor_1_res), .out(RESULT), .sel(NOR));
  _21TH_BIT u_21th_bit_1 (.INPUT(RESULT), ._21TH_BIT(NEGATIVE));
  REDUCED_OR reduced_or_1 (.INPUT(RESULT), .OUTPUT(ZERO));

  // Notes on the sheet:
  //   A
  //   B
  //   AND
  //   OR
  //   ADD/SUB
  //   2107118
  //   21TH BIT
  //   REDUCED_OR
endmodule

module ADDER_1_BIT (
  input  A,
  input  B,
  input  C,
  output OUTPUT,
  output CARRY_OUT
);

  wire and_1_out, and_2_out, xor_1_out;

  xor xor_1 (xor_1_out, A, B);
  and and_1 (and_1_out, A, B);
  and and_2 (and_2_out, C, xor_1_out);
  xor xor_2 (OUTPUT, xor_1_out, C);
  or or_1 (CARRY_OUT, and_2_out, and_1_out);

  // Notes on the sheet:
  //   2107118
endmodule

module _22_BIT_OR (
  input  [21:0] A,
  input  [21:0] B,
  output [21:0] RESULT
);

  or _1 (RESULT[0], A[0], B[0]);
  or _2 (RESULT[1], A[1], B[1]);
  or _3 (RESULT[2], A[2], B[2]);
  or _4 (RESULT[3], A[3], B[3]);
  or _5 (RESULT[4], A[4], B[4]);
  or _6 (RESULT[5], A[5], B[5]);
  or _7 (RESULT[6], A[6], B[6]);
  or _8 (RESULT[7], A[7], B[7]);
  or _9 (RESULT[8], A[8], B[8]);
  or _10 (RESULT[9], A[9], B[9]);
  or _11 (RESULT[10], A[10], B[10]);
  or _12 (RESULT[11], A[11], B[11]);
  or _13 (RESULT[12], A[12], B[12]);
  or _14 (RESULT[13], A[13], B[13]);
  or _15 (RESULT[14], A[14], B[14]);
  or _16 (RESULT[15], A[15], B[15]);
  or _17 (RESULT[16], A[16], B[16]);
  or _18 (RESULT[17], A[17], B[17]);
  or _19 (RESULT[18], A[18], B[18]);
  or _20 (RESULT[19], A[19], B[19]);
  or _21 (RESULT[20], A[20], B[20]);
  or _22 (RESULT[21], A[21], B[21]);

  // Other names for the same wires on the sheet: _11 = A[11]; _12 = A[12]; _13 = A[13]; _14 = A[14]; _15 = A[15];
  //   _16 = A[16]; _17 = A[17]; _18 = A[18]; _19 = A[19]; _20 = A[20]; _21 = A[21]

  // Notes on the sheet:
  //   2107118
endmodule

module _22_BIT_AND (
  input  [21:0] A,
  input  [21:0] B,
  output [21:0] RESULT
);

  and _1 (RESULT[0], A[0], B[0]);
  and _2 (RESULT[1], A[1], B[1]);
  and _3 (RESULT[2], A[2], B[2]);
  and _4 (RESULT[3], A[3], B[3]);
  and _5 (RESULT[4], A[4], B[4]);
  and _6 (RESULT[5], A[5], B[5]);
  and _7 (RESULT[6], A[6], B[6]);
  and _8 (RESULT[7], A[7], B[7]);
  and _9 (RESULT[8], A[8], B[8]);
  and _10 (RESULT[9], A[9], B[9]);
  and _11 (RESULT[10], A[10], B[10]);
  and _12 (RESULT[11], A[11], B[11]);
  and _13 (RESULT[12], A[12], B[12]);
  and _14 (RESULT[13], A[13], B[13]);
  and _15 (RESULT[14], A[14], B[14]);
  and _16 (RESULT[15], A[15], B[15]);
  and _17 (RESULT[16], A[16], B[16]);
  and _18 (RESULT[17], A[17], B[17]);
  and _19 (RESULT[18], A[18], B[18]);
  and _20 (RESULT[19], A[19], B[19]);
  and _21 (RESULT[20], A[20], B[20]);
  and _22 (RESULT[21], A[21], B[21]);

  // Other names for the same wires on the sheet: _011 = A[11]; _012 = A[12]; _013 = A[13]; _014 = A[14]; _015 = A[15];
  //   _016 = A[16]; _017 = A[17]; _018 = A[18]; _019 = A[19]; _020 = A[20]; _021 = A[21]; B011 = B[11]; B012 = B[12];
  //   B013 = B[13]; B014 = B[14]; B015 = B[15]; B016 = B[16]; B017 = B[17]; B018 = B[18]; B019 = B[19]; B020 = B[20];
  //   B021 = B[21]

  // Notes on the sheet:
  //   2107118
endmodule

module _22_BIT_ADDER_SUBTRACTOR (
  input  C_IN,
  input  [21:0] A,
  input  [21:0] B,
  output [21:0] RESULT,
  output CARRY_OUT,
  output OVERFLOW
);

  wire _1_out, _2_out, _3_out, _4_out, _5_out, _6_out, _7_out, _8_out, _9_out, _10_out, _11_out, _12_out,
       _13_out, _14_out, _15_out, _16_out, _17_out, _18_out, _19_out, _20_out, _21_out, _22_out, A_minus_out,
       adder_1_bit_1_carry_out, adder_1_bit_2_carry_out, adder_1_bit_3_carry_out, adder_1_bit_4_carry_out,
       adder_1_bit_5_carry_out, adder_1_bit_6_carry_out, adder_1_bit_7_carry_out, adder_1_bit_8_carry_out,
       adder_1_bit_9_carry_out, adder_1_bit_10_carry_out, adder_1_bit_11_carry_out, adder_1_bit_12_carry_out,
       adder_1_bit_13_carry_out, adder_1_bit_14_carry_out, adder_1_bit_15_carry_out,
       adder_1_bit_16_carry_out, adder_1_bit_17_carry_out, adder_1_bit_18_carry_out,
       adder_1_bit_19_carry_out, adder_1_bit_20_carry_out, adder_1_bit_21_carry_out, and_1_out, and_2_out,
       B_minus_out, R_minus_out;

  xor _1 (_1_out, C_IN, B[0]);
  xor _2 (_2_out, C_IN, B[1]);
  xor _3 (_3_out, C_IN, B[2]);
  xor _4 (_4_out, C_IN, B[3]);
  xor _5 (_5_out, C_IN, B[4]);
  xor _6 (_6_out, C_IN, B[5]);
  xor _7 (_7_out, C_IN, B[6]);
  xor _8 (_8_out, C_IN, B[7]);
  xor _9 (_9_out, C_IN, B[8]);
  xor _10 (_10_out, C_IN, B[9]);
  xor _11 (_11_out, C_IN, B[10]);
  xor _12 (_12_out, C_IN, B[11]);
  xor _13 (_13_out, C_IN, B[12]);
  xor _14 (_14_out, C_IN, B[13]);
  xor _15 (_15_out, C_IN, B[14]);
  buf _16 (_16_out, C_IN);  // XOR_Gate
  xor _17 (_17_out, C_IN, B[16]);
  xor _18 (_18_out, C_IN, B[17]);
  xor _19 (_19_out, C_IN, B[18]);
  xor _20 (_20_out, C_IN, B[19]);
  xor _21 (_21_out, C_IN, B[20]);
  xor _22 (_22_out, C_IN, B[21]);
  not A_minus (A_minus_out, A[21]);
  not B_minus (B_minus_out, _22_out);
  not R_minus (R_minus_out, RESULT[21]);
  and and_1 (and_1_out, RESULT[21], B_minus_out, A_minus_out);
  and and_2 (and_2_out, R_minus_out, _22_out, A[21]);
  ADDER_1_BIT adder_1_bit_1 (.A(C_IN), .B(A[0]), .C(_1_out), .OUTPUT(RESULT[0]), .CARRY_OUT(adder_1_bit_1_carry_out));
  ADDER_1_BIT adder_1_bit_2 (
    .A(adder_1_bit_1_carry_out), .B(A[1]), .C(_2_out), .OUTPUT(RESULT[1]), .CARRY_OUT(adder_1_bit_2_carry_out));
  ADDER_1_BIT adder_1_bit_3 (
    .A(adder_1_bit_2_carry_out), .B(A[2]), .C(_3_out), .OUTPUT(RESULT[2]), .CARRY_OUT(adder_1_bit_3_carry_out));
  ADDER_1_BIT adder_1_bit_4 (
    .A(adder_1_bit_3_carry_out), .B(A[3]), .C(_4_out), .OUTPUT(RESULT[3]), .CARRY_OUT(adder_1_bit_4_carry_out));
  ADDER_1_BIT adder_1_bit_5 (
    .A(adder_1_bit_4_carry_out), .B(A[4]), .C(_5_out), .OUTPUT(RESULT[4]), .CARRY_OUT(adder_1_bit_5_carry_out));
  ADDER_1_BIT adder_1_bit_6 (
    .A(adder_1_bit_5_carry_out), .B(A[5]), .C(_6_out), .OUTPUT(RESULT[5]), .CARRY_OUT(adder_1_bit_6_carry_out));
  ADDER_1_BIT adder_1_bit_7 (
    .A(adder_1_bit_6_carry_out), .B(A[6]), .C(_7_out), .OUTPUT(RESULT[6]), .CARRY_OUT(adder_1_bit_7_carry_out));
  ADDER_1_BIT adder_1_bit_8 (
    .A(adder_1_bit_7_carry_out), .B(A[7]), .C(_8_out), .OUTPUT(RESULT[7]), .CARRY_OUT(adder_1_bit_8_carry_out));
  ADDER_1_BIT adder_1_bit_9 (
    .A(adder_1_bit_8_carry_out), .B(A[8]), .C(_9_out), .OUTPUT(RESULT[8]), .CARRY_OUT(adder_1_bit_9_carry_out));
  ADDER_1_BIT adder_1_bit_10 (
    .A(adder_1_bit_9_carry_out), .B(A[9]), .C(_10_out), .OUTPUT(RESULT[9]),
    .CARRY_OUT(adder_1_bit_10_carry_out));
  ADDER_1_BIT adder_1_bit_11 (
    .A(adder_1_bit_10_carry_out), .B(A[10]), .C(_11_out), .OUTPUT(RESULT[10]),
    .CARRY_OUT(adder_1_bit_11_carry_out));
  ADDER_1_BIT adder_1_bit_12 (
    .A(adder_1_bit_11_carry_out), .B(A[11]), .C(_12_out), .OUTPUT(RESULT[11]),
    .CARRY_OUT(adder_1_bit_12_carry_out));
  ADDER_1_BIT adder_1_bit_13 (
    .A(adder_1_bit_12_carry_out), .B(A[12]), .C(_13_out), .OUTPUT(RESULT[12]),
    .CARRY_OUT(adder_1_bit_13_carry_out));
  ADDER_1_BIT adder_1_bit_14 (
    .A(adder_1_bit_13_carry_out), .B(A[13]), .C(_14_out), .OUTPUT(RESULT[13]),
    .CARRY_OUT(adder_1_bit_14_carry_out));
  ADDER_1_BIT adder_1_bit_15 (
    .A(adder_1_bit_14_carry_out), .B(A[14]), .C(_15_out), .OUTPUT(RESULT[14]),
    .CARRY_OUT(adder_1_bit_15_carry_out));
  ADDER_1_BIT adder_1_bit_16 (
    .A(adder_1_bit_15_carry_out), .B(A[15]), .C(_16_out), .OUTPUT(RESULT[15]),
    .CARRY_OUT(adder_1_bit_16_carry_out));
  ADDER_1_BIT adder_1_bit_17 (
    .A(adder_1_bit_16_carry_out), .B(A[16]), .C(_17_out), .OUTPUT(RESULT[16]),
    .CARRY_OUT(adder_1_bit_17_carry_out));
  ADDER_1_BIT adder_1_bit_18 (
    .A(adder_1_bit_17_carry_out), .B(A[17]), .C(_18_out), .OUTPUT(RESULT[17]),
    .CARRY_OUT(adder_1_bit_18_carry_out));
  ADDER_1_BIT adder_1_bit_19 (
    .A(adder_1_bit_18_carry_out), .B(A[18]), .C(_19_out), .OUTPUT(RESULT[18]),
    .CARRY_OUT(adder_1_bit_19_carry_out));
  ADDER_1_BIT adder_1_bit_20 (
    .A(adder_1_bit_19_carry_out), .B(A[19]), .C(_20_out), .OUTPUT(RESULT[19]),
    .CARRY_OUT(adder_1_bit_20_carry_out));
  ADDER_1_BIT adder_1_bit_21 (
    .A(adder_1_bit_20_carry_out), .B(A[20]), .C(_21_out), .OUTPUT(RESULT[20]),
    .CARRY_OUT(adder_1_bit_21_carry_out));
  ADDER_1_BIT adder_1_bit_22 (
    .A(adder_1_bit_21_carry_out), .B(A[21]), .C(_22_out), .OUTPUT(RESULT[21]), .CARRY_OUT(CARRY_OUT));
  or or_1 (OVERFLOW, and_1_out, and_2_out);

  // Other names for the same wires on the sheet: CONTROL = C_IN

  // Notes on the sheet:
  //   2107118
endmodule

module REDUCED_OR (
  input  [21:0] INPUT,
  output OUTPUT
);

  wire _22BIT_out;

  or _22BIT (_22BIT_out, INPUT[0], INPUT[1], INPUT[2], INPUT[3], INPUT[4], INPUT[5], INPUT[6], INPUT[7], INPUT[8], INPUT[9], INPUT[10], INPUT[11], INPUT[12], INPUT[13], INPUT[14], INPUT[15], INPUT[16], INPUT[17], INPUT[18], INPUT[19], INPUT[20], INPUT[21]);
  not not_1 (OUTPUT, _22BIT_out);

  // Notes on the sheet:
  //   2107118
endmodule

module _21TH_BIT (
  input  [21:0] INPUT,
  output _21TH_BIT
);


  assign _21TH_BIT = INPUT[21];

  // Notes on the sheet:
  //   2107118
endmodule

module HOMEWORK (
  input  ADD_SUB,
  input  in_2,
  input  in_3,
  input  OUTPUT,
  input  in_5,
  input  in_6,
  input  in_7,
  input  in_8,
  input  in_9,
  output CARRYOUT
);

  wire CLOCK_out;
  wire [21:0] A_q, AA, B_q, BB, C_q, CC, D_q, DD, multiplexer_1_out, multiplexer_2_out,
       n22_bit_adder_subtractor_1_result;

  Register #(.width(22)) A (.D(AA), .en(in_5), .Q(A_q), .clk(CLOCK_out), .clr(in_2));
  Register #(.width(22)) B (.D(BB), .en(in_5), .Q(B_q), .clk(CLOCK_out), .clr(in_2));
  Register #(.width(22)) C (.D(CC), .en(in_5), .Q(C_q), .clk(CLOCK_out), .clr(in_2));
  Register #(.width(22)) D (.D(DD), .en(in_5), .Q(D_q), .clk(CLOCK_out), .clr(in_2));
  Clock CLOCK (.out(CLOCK_out));
  Multiplexer #(.select(2), .width(22)) multiplexer_1 (
    .in0(A_q), .in1(B_q), .in2(C_q), .in3(D_q), .out(multiplexer_1_out), .sel({in_8, in_9}));  // open: en
  Multiplexer #(.select(2), .width(22)) multiplexer_2 (
    .in0(A_q), .in1(B_q), .in2(C_q), .in3(D_q), .out(multiplexer_2_out), .sel({in_6, in_7}));  // open: en
  _22_BIT_ADDER_SUBTRACTOR u_22_bit_adder_subtractor_1 (
    .A(multiplexer_1_out), .B(multiplexer_2_out), .C_IN(ADD_SUB), .RESULT(n22_bit_adder_subtractor_1_result),
    .CARRY_OUT(CARRYOUT));  // open: OVERFLOW
  Demultiplexer #(.select(2), .width(22)) demultiplexer_1 (
    .out0(AA), .out1(BB), .out2(CC), .out3(DD), .in(n22_bit_adder_subtractor_1_result), .sel({in_3, OUTPUT}));  // open: en

  // Notes on the sheet:
  //   B
  //   A
  //   ADDER
endmodule

// NAND
module \xnor  (
  input  [21:0] A,
  input  [21:0] B,
  output [21:0] RESUL
);

  wire [21:0] nand_1_out;

  assign nand_1_out = ~(A & B);  // NAND_Gate nand_1, 22 bits wide
endmodule

module NOR (
  input  [21:0] A,
  input  [21:0] B,
  output [21:0] RES
);

  assign RES = ~(A | B);  // NOR_Gate nor_1, 22 bits wide
endmodule
