// Logisim project CPU CIRCUIT.circ as structural Verilog: 3 circuits, main circuit main
module main (
  input  RESET
);

  wire CLOCK_out, cpu_circuit_1_r, cpu_circuit_1_w;
  wire [17:0] cpu_circuit_1_address;
  wire [21:0] cpu_circuit_1_dataout, ram_1_data;

  Clock CLOCK (.out(CLOCK_out));
  CPU_CIRCUIT cpu_circuit_1 (
    .CLOCK(CLOCK_out), .RESET(RESET), .W(cpu_circuit_1_w), .R(cpu_circuit_1_r),
    .ADDRESS(cpu_circuit_1_address), .DATAIN(ram_1_data), .DATAOUT(cpu_circuit_1_dataout));
  RAM #(.addrWidth(18), .dataWidth(22), .bus("separate")) ram_1 (
    .addr(cpu_circuit_1_address), .din(cpu_circuit_1_dataout), .data(ram_1_data), .str(cpu_circuit_1_w),
    .clk(CLOCK_out), .ld(cpu_circuit_1_r));  // open: sel, clr

  // Notes on the sheet:
  //   0-->AND
  //   1-->ADD
  //   2-->STORE
  //   3-->OR
  //   4-->SUB
  //   5-->JUMP
  //   6-->LOAD
  //   7-->XNOR
  //   8-->HALT
  //   2107118
endmodule

// CPU
module CPU_CIRCUIT (
  input  CLOCK,
  input  RESET,
  input  [21:0] DATAIN,
  output W,
  output R,
  output [17:0] ADDRESS,
  output [21:0] DATAOUT
);

  wire B1, C0, C1, CC1, CC2, control_unit_design_1_nand, control_unit_design_1_nor, D1, D2, LDAC,
       LOADA_FROM_MBR, LOADAC, LOADB, LOADMAR;
  wire [17:0] multiplexer_1_out, PC_q;
  wire [21:0] AC, ACIN, ALU_OUT, multiplexer_3_out;

  Multiplexer #(.width(18)) multiplexer_1 (
    .in0(PC_q), .in1(DATAOUT[17:0]), .out(multiplexer_1_out), .sel(D2));  // open: en
  CONTROL_UNIT_DESIGN control_unit_design_1 (
    .IR(DATAOUT[21:18]), .CLOCK(CLOCK), .RESET(RESET), .OPERATION({C0, C1}), .D1(D1), .C1(CC1), .R(R),
    .C2(CC2), .D2(D2), .B1(B1), .LOAD_AC(LDAC), .W(W), .NAND(control_unit_design_1_nand),
    .NOR(control_unit_design_1_nor), .LOADAFRB(LOADA_FROM_MBR));
  Counter #(.width(18), .max('h3ffff)) PC (
    .load(CC2), .D(DATAOUT[17:0]), .count(CC1), .Q(PC_q), .clk(CLOCK), .clr(RESET));  // open: carry
  Register #(.width(18)) MAR (.D(multiplexer_1_out), .en(LOADMAR), .Q(ADDRESS), .clk(CLOCK), .clr(RESET));
  Register #(.width(4)) IR (.D(DATAOUT[21:18]), .en(CC1), .clk(CLOCK), .clr(RESET));  // open: Q
  Multiplexer #(.width(22)) multiplexer_2 (.in0(ALU_OUT), .in1(DATAOUT), .out(ACIN), .sel(LOADA_FROM_MBR));  // open: en
  Multiplexer #(.width(22)) multiplexer_3 (.in0(DATAIN), .in1(AC), .out(multiplexer_3_out), .sel(B1));  // open: en
  or or_1 (LOADB, B1, R);
  or or_2 (LOADAC, LOADA_FROM_MBR, LDAC);
  or or_3 (LOADMAR, D1, D2);
  Register #(.width(22)) MBR (.D(multiplexer_3_out), .en(LOADB), .Q(DATAOUT), .clk(CLOCK), .clr(RESET));
  Register #(.width(22)) ACUMULATOR (.D(ACIN), .en(LOADAC), .Q(AC), .clk(CLOCK), .clr(RESET));
  _2107118_ALU_22_BIT_main main_1 (
    .A(AC), .NAND(control_unit_design_1_nand), .B(DATAOUT), .NOR(control_unit_design_1_nor), .CONTROL_0(C1),
    .CONTROL_1(C0), .RESULT(ALU_OUT));  // open: ZERO, NEGATIVE, CARRY, OVERFLOW

  // Other names for the same wires on the sheet: CLR = RESET; MBROUT[21:0] = DATAOUT; MBR4BIT[3:0] = DATAOUT[21:18]
endmodule

// CU
module CONTROL_UNIT_DESIGN (
  input  [3:0] IR,
  input  CLOCK,
  input  RESET,
  output D1,
  output C1,
  output R,
  output C2,
  output D2,
  output [1:0] OPERATION,
  output B1,
  output LOAD_AC,
  output W,
  output NAND,
  output NOR,
  output LOADAFRB
);

  wire and_1_out, decoder_1_out6, decoder_1_out7, decoder_1_out8, decoder_1_out9, decoder_1_out15, not_1_out,
       or_1_out;
  wire [5:0] counter_1_q;
  wire [6:0] rom_1_data;

  Counter #(.width(6), .max('h3f)) counter_1 (
    .load(rom_1_data[2]), .D({IR, 2'b11}), .count(rom_1_data[0]), .Q(counter_1_q), .clk(and_1_out),
    .clr(or_1_out));  // open: carry
  and and_1 (and_1_out, CLOCK, not_1_out);
  or or_1 (or_1_out, RESET, rom_1_data[1]);
  ROM #(.addrWidth(6), .dataWidth(7)) rom_1 (.addr(counter_1_q), .data(rom_1_data));  // open: sel
  Decoder #(.select(4), .enable("false")) decoder_1 (
    .out1(D1), .out2(C1), .out3(R), .out4(C2), .out5(D2), .out6(decoder_1_out6), .out7(decoder_1_out7),
    .out8(decoder_1_out8), .out9(decoder_1_out9), .out10(B1), .out11(W), .out12(NAND), .out13(NOR),
    .out14(LOADAFRB), .out15(decoder_1_out15), .sel(rom_1_data[6:3]));  // open: out0
  not not_1 (not_1_out, decoder_1_out15);
  Priority_Encoder #(.select(2)) priority_encoder_1 (
    .in0(decoder_1_out6), .in1(decoder_1_out7), .in2(decoder_1_out8), .in3(decoder_1_out9), .out(OPERATION));  // open: gs, en_out, en_in
  or or_2 (LOAD_AC, decoder_1_out6, decoder_1_out7, decoder_1_out8, decoder_1_out9);

  // Notes on the sheet:
  //   contents of rom_1 (hex, n*v repeats v):
  //   9 19 14 29 19 31 2 29 19 39 2 29 51 59 2 29 19 41 2 29 19 49 2 21 2 2 2 29 19 71 2 29 19 61 2 78
endmodule
